# Fritzing sketch Mini Hydrophonics Schematic (saved by Fritzing 1.0.6)

parts:
  Relays = 6 channel relay module
  Arduino_Mega = Arduino Mega 2560 (Rev3)
  U1 = LM2596 step down module
  J3 = Camdenboss CTB0158-2 [part_number=CTB0158-2 package=THT]
  J4 = Camdenboss CTB0158-2 [part_number=CTB0158-2 package=THT]
  J5 = Camdenboss CTB0158-2 [part_number=CTB0158-2 package=THT]
  J6 = Camdenboss CTB0158-2 [part_number=CTB0158-2 package=THT]
  J7 = Camdenboss CTB0158-2 [part_number=CTB0158-2 package=THT]
  J8 = Camdenboss CTB0158-2 [part_number=CTB0158-2 package=THT]
  Grow_Light = 60mm 8x8 dot matrix column cathode led display with standard pcb pads
  pH_Down_WPump = water pump/motor
  Nutrient_Mix_WPump = water pump/motor
  WReservoir_WPump = water pump/motor
  Mixer = DC Motor [voltage_(max)=6V voltage_(min)=3V]
  PUMP_-_GC = water pump/motor
  M1 = PH meter with sensor in breadboard [package=THT]
  Water_Level_Sensor = HC-SR04 Ultrasonic Distance Sensor
  A1 = tds-sensor-meter-v1.0_1
  J14 = Wago 221-413
  +24_V_Splicer = Wago 221-413
  J15 = Wago 221-413
  BAT1 = 24 battery [package=battery]
  -24_V_Splicer = Wago 221-413

nets:
  N1: Relays.Pin_2, Arduino_Mega.D13_PWM
  N2: Relays.Pin_3, Arduino_Mega.D12_PWM
  N3: Relays.Pin_4, Arduino_Mega.D11_PWM
  N4: Relays.Pin_5, Arduino_Mega.D10_PWM
  N5: Relays.Pin_6, Arduino_Mega.D9_PWM
  N6: Relays.Pin_7, Arduino_Mega.D8_PWM
  GND: Relays.Pin_12, Arduino_Mega.GND, U1.IN-, U1.OUT-, M1.pin3, Water_Level_Sensor.GND, A1.pin3, J14.Pin_1, J14.Pin_2, J14.Pin_3, BAT1.-, -24_V_Splicer.Pin_1, -24_V_Splicer.Pin_2, -24_V_Splicer.Pin_3
  N7: Relays.Pin_13, J3.pin1
  N8: Relays.Pin_16, J4.pin1
  N9: Relays.Pin_19, J5.pin1
  N10: Relays.Pin_22, J6.pin1
  N11: Relays.Pin_25, J7.pin1
  N12: Relays.Pin_28, J8.pin1
  N13: Arduino_Mega.A0, M1.pin1
  N14: Arduino_Mega.A1, A1.pin1
  5V: Arduino_Mega.5V, U1.OUT+, M1.pin2, Water_Level_Sensor.VCC, A1.pin2, J15.Pin_1, J15.Pin_2, J15.Pin_3
  N15: Arduino_Mega.D41, Water_Level_Sensor.TRIG
  N16: Arduino_Mega.D43, Water_Level_Sensor.ECHO
  N17: U1.IN+, J3.pin2, +24_V_Splicer.Pin_1, +24_V_Splicer.Pin_2, +24_V_Splicer.Pin_3, BAT1.+
  N18: J3.terminal_1, Grow_Light.pin_1
  N19: J3.terminal_2, Grow_Light.pin_2
  N20: J4.terminal_1, pH_Down_WPump.pin_2
  N21: J4.terminal_2, pH_Down_WPump.pin_1
  N22: J5.terminal_1, Nutrient_Mix_WPump.pin_2
  N23: J5.terminal_2, Nutrient_Mix_WPump.pin_1
  N24: J6.terminal_1, WReservoir_WPump.pin_2
  N25: J6.terminal_2, WReservoir_WPump.pin_1
  N26: J7.terminal_1, Mixer.pin_1
  N27: J7.terminal_2, Mixer.pin_2
  N28: J8.terminal_1, PUMP_-_GC.pin_2
  N29: J8.terminal_2, PUMP_-_GC.pin_1

custom parts:
  6 channel relay module: 6 Channel 5V Relay Board Module Optocoupler LED.
  LM2596 step down module: LM2596 DC-DC step down power supply module 3 A.
  water pump/motor: WATER PUMP BY ARDUBLOCKTR
  PH meter with sensor in breadboard: DFrobot PH meter (SKU SEN0161)
  : TDS Meter V1.0 Development Board Water Meter Filter Measuring Water Sensor Module.
  Wago 221-413: Wago 221-413 3 position splicing connector 12AWG.
  24 battery: 24V lead acid type battery, like the Husqvarna YTH2448 12V 35AH battery. This is the mini version 1/4 the size of the actual battery to be closer to typical breadboard parts (around 2in wide rathher than 7in). The pads in pcb are sized to accomidate up to 14ga wire (as these batterys will deliver high currents.)
